// Logisim project Lab-2.circ as structural Verilog: 1 circuit, main circuit main
module main (
  input  A,
  input  B,
  input  C,
  input  A_2,
  input  B_2,
  input  C_2,
  output out_7,
  output out_8
);

  wire and_1_out, and_3_out, and_4_out, and_5_out, not_1_out, not_2_out, not_3_out, not_4_out, not_5_out,
       not_6_out, or_1_out, or_2_out, or_3_out, or_4_out, or_5_out;

  not not_1 (not_1_out, A);
  not not_2 (not_2_out, B);
  not not_3 (not_3_out, C);
  or or_1 (or_1_out, A, B, C);
  or or_2 (or_2_out, A, not_2_out, not_3_out);
  or or_3 (or_3_out, not_1_out, B, C);
  or or_4 (or_4_out, not_1_out, B, not_3_out);
  or or_5 (or_5_out, not_1_out, not_2_out, not_3_out);
  and and_1 (and_1_out, or_1_out, or_2_out, or_3_out);
  and and_2 (out_7, and_1_out, or_4_out, or_5_out);
  not not_4 (not_4_out, A_2);
  not not_5 (not_5_out, B_2);
  not not_6 (not_6_out, C_2);
  and and_3 (and_3_out, not_4_out, not_5_out, C_2);
  and and_4 (and_4_out, not_4_out, B_2, not_6_out);
  and and_5 (and_5_out, A_2, B_2, not_6_out);
  or or_6 (out_8, and_3_out, and_4_out, and_5_out);

  // Notes on the sheet:
  //   4075
  //   4073
  //   4073
  //   2nd Canonical Form
  //   4073
  //   4073
  //   4073
  //   Shakil Ahmed
  //   ID: 2221453042
  //   CSE231.9
  //   Faculty Initial: OISD
  //   Lab Instructor: Pritthika Dhar
  //   1st Canonical Form
  //   4075
endmodule
